// Logisim project test.circ as structural Verilog: 1 circuit, main circuit main
module main (
);

  wire clock_1_out;

  Clock clock_1 (.out(clock_1_out));
  D_Flip_Flop d_ff_1 ();  // open: clk, D, Q, Qn, preset, reset
endmodule
