// Logisim project VideoDriver.circ as structural Verilog: 2 circuits, main circuit main
module main (
);

  wire button_1_out, Char_Column_carry, clock_1_out, clock_2_out, counter_4_carry, multiplexer_1_out,
       multiplexer_2_out, rgb_video_1_p2, X_Char_carry, Y_Char_carry;
  wire [2:0] Char_Column_q, rgb_video_1_p7, rgb_video_2_p5, rgb_video_2_p5_2, rgb_video_2_p7, undriven,
       X_Char_q;
  wire [3:3] Char_Row_q, rgb_video_2_p6;
  wire [7:0] Char_Generator_data, rom_1_data, rom_2_data, VRAM_data;

  Counter #(.max('h7), .trigger("falling"), .width(3)) Char_Column (
    .Q(Char_Column_q), .carry(Char_Column_carry), .clk(X_Char_carry));  // open: load, D, count, up, clr
  Counter #(.max('h1), .trigger("falling"), .width(1)) Char_Row (
    .Q(Char_Row_q[3]), .clk(Y_Char_carry));  // open: load, D, count, carry, up, clr
  ROM Char_Generator (.addr(VRAM_data), .data(Char_Generator_data));
  ROM rom_1 (.addr(rom_2_data), .data(rom_1_data));
  ROM #(.addrWidth(4), .dataWidth(5)) VRAM (.addr({Char_Row_q[3], Char_Column_q}), .data(VRAM_data[7:3]));
  ROM #(.addrWidth(4), .dataWidth(5)) rom_2 (.addr({rgb_video_2_p6[3], rgb_video_2_p5_2}), .data(rom_2_data[7:3]));
  Clock clock_1 (.out(clock_1_out));
  Clock clock_2 (.out(clock_2_out));
  Multiplexer #(.select(3)) multiplexer_1 (
    .in0(Char_Generator_data[7]), .in1(Char_Generator_data[6]), .in2(Char_Generator_data[5]),
    .in3(Char_Generator_data[4]), .in4(Char_Generator_data[3]), .in5(Char_Generator_data[2]),
    .in6(Char_Generator_data[1]), .in7(Char_Generator_data[0]), .out(multiplexer_1_out), .sel(X_Char_q));
  Multiplexer #(.select(3)) multiplexer_2 (
    .in0(rom_1_data[7]), .in1(rom_1_data[6]), .in2(rom_1_data[5]), .in3(rom_1_data[4]), .in4(rom_1_data[3]),
    .in5(rom_1_data[2]), .in6(rom_1_data[1]), .in7(rom_1_data[0]), .out(multiplexer_2_out),
    .sel(rgb_video_2_p5));
  T_Flip_Flop t_ff_1 (.T(1'b1));  // open: clk, Q, Qn, preset, reset
  Counter #(.max('h7), .trigger("falling"), .width(3)) X_Char (
    .Q(X_Char_q), .carry(X_Char_carry), .clk(clock_1_out));  // open: load, D, count, up, clr
  Counter #(.max('h7), .trigger("falling"), .width(3)) Y_Char (
    .Q(VRAM_data[2:0]), .carry(Y_Char_carry), .clk(Char_Column_carry));  // open: load, D, count, up, clr
  Button button_1 (.out(button_1_out));
  // RGB_Video #(.height(16), .scale(8), .width(64)) rgb_video_1: pin names not known; wires that end beside it: clock_1_out, rgb_video_1_p2, clock_1_out, 1'b1, {Char_Column_q, X_Char_q}, {Char_Row_q[3], VRAM_data[2:0]}, rgb_video_1_p7
  Button button_2 (.out(rgb_video_1_p2));
  // Probe on {Char_Column_q, X_Char_q}
  // Probe on {Char_Row_q[3], VRAM_data[2:0]}
  // RGB_Video #(.height(16), .scale(8), .width(64)) rgb_video_2: pin names not known; wires that end beside it: clock_2_out, button_1_out, clock_2_out, 1'b1, {rgb_video_2_p5_2, rgb_video_2_p5}, {rgb_video_2_p6[3], rom_2_data[2:0]}, rgb_video_2_p7
  // Probe on {rgb_video_2_p5_2, rgb_video_2_p5}
  // Probe on {rgb_video_2_p6[3], rom_2_data[2:0]}
  Multiplexer #(.width(3)) multiplexer_3 (.in0(3'b000), .in1(undriven), .out(rgb_video_2_p7), .sel(multiplexer_2_out));
  Multiplexer #(.width(3)) multiplexer_4 (.in0(3'b000), .in1(3'b010), .out(rgb_video_1_p7), .sel(multiplexer_1_out));
  Counter #(.max('h1), .trigger("falling"), .width(1)) counter_1 ();  // open: load, D, count, Q, carry, up, clk, clr
  Counter #(.max('h7), .trigger("falling"), .width(3)) counter_2 ();  // open: load, D, count, Q, carry, up, clk, clr
  Counter #(.max('h7), .trigger("falling"), .width(3)) counter_3 (.clk(counter_4_carry));  // open: load, D, count, Q, carry, up, clr
  Counter #(.max('h7), .trigger("falling"), .width(3)) counter_4 (.carry(counter_4_carry));  // open: load, D, count, Q, up, clk, clr

  // Notes on the sheet:
  //   contents of Char_Generator (hex, n*v repeats v):
  //   8*0 84 84 84 fc 84 84 84 0 fc 80 80 f0 80 80 fc 0 6*80 fc 0 78 5*84 78
  //   contents of rom_1 (hex, n*v repeats v):
  //   8*0 84 84 84 fc 84 84 84 0 fc 80 80 f0 80 80 fc 0 6*80 fc 0 78 5*84 78
  //   contents of VRAM (hex, n*v repeats v):
  //   3 1 4 3 4*0 1 2 3 3 4
  //   contents of rom_2 (hex, n*v repeats v):
  //   0 3 4 3 4*0 1 2 3 3 4
endmodule

module CNTR (
);

  wire Char_Column_carry, clock_1_out, multiplexer_1_out, rgb_video_1_p1, X_Char_carry, Y_Char_carry;
  wire [2:0] rgb_video_1_p6, X_Char_q;
  wire [3:0] Char_Column_q;
  wire [7:0] Char_Generator_data, VRAM_data;

  ROM #(.addrWidth(4), .dataWidth(5)) VRAM (.addr(Char_Column_q), .data(VRAM_data[7:3]));
  ROM Char_Generator (.addr(VRAM_data), .data(Char_Generator_data));
  Multiplexer #(.select(3)) multiplexer_1 (
    .in0(Char_Generator_data[7]), .in1(Char_Generator_data[6]), .in2(Char_Generator_data[5]),
    .in3(Char_Generator_data[4]), .in4(Char_Generator_data[3]), .in5(Char_Generator_data[2]),
    .in6(Char_Generator_data[1]), .in7(Char_Generator_data[0]), .out(multiplexer_1_out), .sel(X_Char_q));
  Clock clock_1 (.out(clock_1_out));
  Counter #(.max('h1), .trigger("falling"), .width(1)) Char_Row (
    .Q(Char_Column_q[3]), .clk(Y_Char_carry));  // open: load, D, count, carry, up, clr
  Counter #(.max('h7), .trigger("falling"), .width(3)) Y_Char (
    .Q(VRAM_data[2:0]), .carry(Y_Char_carry), .clk(Char_Column_carry));  // open: load, D, count, up, clr
  Counter #(.max('h7), .trigger("falling"), .width(3)) Char_Column (
    .Q(Char_Column_q[2:0]), .carry(Char_Column_carry), .clk(X_Char_carry));  // open: load, D, count, up, clr
  Counter #(.max('h7), .trigger("falling"), .width(3)) X_Char (
    .Q(X_Char_q), .carry(X_Char_carry), .clk(clock_1_out));  // open: load, D, count, up, clr
  // RGB_Video #(.height(16), .scale(8), .width(64)) rgb_video_1: pin names not known; wires that end beside it: rgb_video_1_p1, clock_1_out, 1'b1, {Char_Column_q[2:0], X_Char_q}, {Char_Column_q[3], VRAM_data[2:0]}, rgb_video_1_p6
  Button button_1 (.out(rgb_video_1_p1));
  // Probe on {Char_Column_q[2:0], X_Char_q}
  // Probe on {Char_Column_q[3], VRAM_data[2:0]}
  Multiplexer #(.width(3)) multiplexer_2 (.in0(3'b000), .in1(3'b011), .out(rgb_video_1_p6), .sel(multiplexer_1_out));

  // Notes on the sheet:
  //   contents of VRAM (hex, n*v repeats v):
  //   0 3 4 3 4*0 1 2 3 3 4
  //   contents of Char_Generator (hex, n*v repeats v):
  //   8*0 84 84 84 fc 84 84 84 0 fc 80 80 f0 80 80 fc 0 6*80 fc 0 78 5*84 78
endmodule
